// Logisim project logisim_24116066.circ as structural Verilog: 15 circuits, main circuit main
module main (
);

  wire beq_t, blt_t, bltu_t, branch_taken_t, clock_t, control_1_reg_we, funct7_t, imm_taken_t, mem_we_t,
       pc_taken_t;
  wire [1:0] reg_write_sel_t;
  wire [2:0] funct3_t;
  wire [3:0] alu_control_1_alusel;
  wire [4:0] rdesi_t, rs1i_t, rs2i_t;
  wire [6:0] op_code_t;
  wire [31:0] A_t, ALU_out_t, B_t, data_mem_1_rd_data, imm_final_t, multiplexer_1_out, pc_next_t, pcplus4_t,
       rd_dataout_t, rs1_t, rs2_t;
  wire [31:25] rom_1_data;

  Clock clock_1 (.out(clock_t));
  ROM #(.addrWidth(16), .dataWidth(32)) rom_1 (
    .addr(pc_next_t[17:2]),
    .data({rom_1_data[31], funct7_t, rom_1_data[29:25], rs2i_t, rs1i_t, funct3_t, rdesi_t, op_code_t}));
  Imm_Gen imm_gen_1 (
    .Instruct({rom_1_data[31], funct7_t, rom_1_data[29:25], rs2i_t, rs1i_t, funct3_t, rdesi_t, op_code_t}),
    .imm(imm_final_t));
  Branch_Comp branch_comp_1 (.A(rs1_t), .B(rs2_t), .beq(beq_t), .blt(blt_t), .bltu(bltu_t));
  ALU_Control alu_control_1 (.opcode(op_code_t), .funct3(funct3_t), .funct7(funct7_t), .ALUSel(alu_control_1_alusel));
  Data_Mem data_mem_1 (
    .WE(mem_we_t), .CLK(clock_t), .funct3(funct3_t), .Rwrite(rs2_t), .addr(ALU_out_t),
    .rd_data(data_mem_1_rd_data));
  Control control_1 (
    .op_code(op_code_t), .funct3(funct3_t), .bltu(beq_t), .blt(blt_t), .beq(bltu_t),
    .reg_write_sel(reg_write_sel_t), .imm_tk(imm_taken_t), .mem_we(mem_we_t), .reg_we(control_1_reg_we),
    .pc_tk(pc_taken_t), .branch_tk(branch_taken_t));
  Multiplexer #(.width(32)) multiplexer_1 (
    .in0(pcplus4_t), .in1(ALU_out_t), .out(multiplexer_1_out), .sel(branch_taken_t));
  Multiplexer #(.select(2), .width(32)) multiplexer_2 (
    .in0(data_mem_1_rd_data), .in1(ALU_out_t), .in2(pcplus4_t), .in3(imm_final_t), .out(rd_dataout_t),
    .sel(reg_write_sel_t));
  Program_Counter program_counter_1 (.PC_in(multiplexer_1_out), .Clock(clock_t), .PC_next(pc_next_t));  // open: reset
  ALU alu_1 (.A(A_t), .B(B_t), .ALUSel(alu_control_1_alusel), .ALUOut(ALU_out_t));
  Multiplexer #(.width(32)) multiplexer_3 (.in0(rs1_t), .in1(pc_next_t), .out(A_t), .sel(pc_taken_t));
  Multiplexer #(.width(32)) multiplexer_4 (.in0(rs2_t), .in1(imm_final_t), .out(B_t), .sel(imm_taken_t));
  PC_plus4 pc_plus4_1 (.PC_in(pc_next_t), .PC_plus_4(pcplus4_t));
  RegFile regfile_1 (
    .Rwrite(rd_dataout_t), .rdesi(rdesi_t), .rs1i(rs1i_t), .rs2i(rs2i_t), .WE(control_1_reg_we),
    .CLK(clock_t), .rs1(rs1_t), .rs2(rs2_t));

  // Notes on the sheet:
  //   contents of rom_1 (hex, n*v repeats v):
  //   10b7 500113 c00193 310233 402182b3 211313 40a023 a383 720463 fff00f93 314463 fff00f93 80046f
  //   fff00f93 2000513 deadc5b7 eef58593 b52023 b51223 b50423 52603 451683 455703 850783 854803 6f
endmodule

module RegFile (
  input  [31:0] Rwrite,
  input  [4:0] rdesi,
  input  [4:0] rs1i,
  input  [4:0] rs2i,
  input  WE,
  input  CLK,
  output [31:0] rs1,
  output [31:0] rs2
);

  wire wesel_0, wesel_1, wesel_2, wesel_3, wesel_4, wesel_5, wesel_6, wesel_7, wesel_8, wesel_9, wesel_10,
       wesel_11, wesel_12, wesel_13, wesel_14, wesel_15, wesel_16, wesel_17, wesel_18, wesel_19, wesel_20,
       wesel_21, wesel_22, wesel_23, wesel_24, wesel_25, wesel_26, wesel_27, wesel_28, wesel_29, wesel_30,
       wesel_31;
  wire [31:0] ri_t1, ri_t2, ri_t3, ri_t4, ri_t5, ri_t6, ri_t7, ri_t8, ri_t9, ri_t10, ri_t11, ri_t12, ri_t13,
       ri_t14, ri_t15, ri_t16, ri_t17, ri_t18, ri_t19, ri_t20, ri_t21, ri_t22, ri_t23, ri_t24, ri_t25,
       ri_t26, ri_t27, ri_t28, ri_t29, ri_t30, ri_t31;

  Register #(.width(32)) register_1 (.D(Rwrite), .en(wesel_5), .clk(CLK), .Q(ri_t5));  // open: clr
  Register #(.width(32)) register_2 (.D(Rwrite), .en(wesel_10), .clk(CLK), .Q(ri_t10));  // open: clr
  Register #(.width(32)) register_3 (.D(Rwrite), .en(wesel_15), .clk(CLK), .Q(ri_t15));  // open: clr
  Register #(.width(32)) register_4 (.D(Rwrite), .en(wesel_20), .clk(CLK), .Q(ri_t20));  // open: clr
  Register #(.width(32)) register_5 (.D(Rwrite), .en(wesel_25), .clk(CLK), .Q(ri_t25));  // open: clr
  Register #(.width(32)) register_6 (.D(Rwrite), .en(wesel_30), .clk(CLK), .Q(ri_t30));  // open: clr
  Register #(.width(32)) register_7 (.D(Rwrite), .en(wesel_1), .clk(CLK), .Q(ri_t1));  // open: clr
  Register #(.width(32)) register_8 (.D(Rwrite), .en(wesel_6), .clk(CLK), .Q(ri_t6));  // open: clr
  Register #(.width(32)) register_9 (.D(Rwrite), .en(wesel_11), .clk(CLK), .Q(ri_t11));  // open: clr
  Register #(.width(32)) register_10 (.D(Rwrite), .en(wesel_16), .clk(CLK), .Q(ri_t16));  // open: clr
  Register #(.width(32)) register_11 (.D(Rwrite), .en(wesel_21), .clk(CLK), .Q(ri_t21));  // open: clr
  Register #(.width(32)) register_12 (.D(Rwrite), .en(wesel_26), .clk(CLK), .Q(ri_t26));  // open: clr
  Register #(.width(32)) register_13 (.D(Rwrite), .en(wesel_31), .clk(CLK), .Q(ri_t31));  // open: clr
  Multiplexer #(.select(5), .width(32)) multiplexer_1 (
    .in0({32{1'b0}}), .in1(ri_t1), .in2(ri_t2), .in3(ri_t3), .in4(ri_t4), .in5(ri_t5), .in6(ri_t6),
    .in7(ri_t7), .in8(ri_t8), .in9(ri_t9), .in10(ri_t10), .in11(ri_t11), .in12(ri_t12), .in13(ri_t13),
    .in14(ri_t14), .in15(ri_t15), .in16(ri_t16), .in17(ri_t17), .in18(ri_t18), .in19(ri_t19), .in20(ri_t20),
    .in21(ri_t21), .in22(ri_t22), .in23(ri_t23), .in24(ri_t24), .in25(ri_t25), .in26(ri_t26), .in27(ri_t27),
    .in28(ri_t28), .in29(ri_t29), .in30(ri_t30), .in31(ri_t31), .out(rs1), .sel(rs1i));
  Register #(.width(32)) register_14 (.D(Rwrite), .en(wesel_2), .clk(CLK), .Q(ri_t2));  // open: clr
  Register #(.width(32)) register_15 (.D(Rwrite), .en(wesel_7), .clk(CLK), .Q(ri_t7));  // open: clr
  Register #(.width(32)) register_16 (.D(Rwrite), .en(wesel_12), .clk(CLK), .Q(ri_t12));  // open: clr
  Register #(.width(32)) register_17 (.D(Rwrite), .en(wesel_17), .clk(CLK), .Q(ri_t17));  // open: clr
  Register #(.width(32)) register_18 (.D(Rwrite), .en(wesel_22), .clk(CLK), .Q(ri_t22));  // open: clr
  Register #(.width(32)) register_19 (.D(Rwrite), .en(wesel_27), .clk(CLK), .Q(ri_t27));  // open: clr
  Multiplexer #(.select(5), .width(32)) multiplexer_2 (
    .in0({32{1'b0}}), .in1(ri_t1), .in2(ri_t2), .in3(ri_t3), .in4(ri_t4), .in5(ri_t5), .in6(ri_t6),
    .in7(ri_t7), .in8(ri_t8), .in9(ri_t9), .in10(ri_t10), .in11(ri_t11), .in12(ri_t12), .in13(ri_t13),
    .in14(ri_t14), .in15(ri_t15), .in16(ri_t16), .in17(ri_t17), .in18(ri_t18), .in19(ri_t19), .in20(ri_t20),
    .in21(ri_t21), .in22(ri_t22), .in23(ri_t23), .in24(ri_t24), .in25(ri_t25), .in26(ri_t26), .in27(ri_t27),
    .in28(ri_t28), .in29(ri_t29), .in30(ri_t30), .in31(ri_t31), .out(rs2), .sel(rs2i));
  Register #(.width(32)) register_20 (.D(Rwrite), .en(wesel_3), .clk(CLK), .Q(ri_t3));  // open: clr
  Register #(.width(32)) register_21 (.D(Rwrite), .en(wesel_8), .clk(CLK), .Q(ri_t8));  // open: clr
  Register #(.width(32)) register_22 (.D(Rwrite), .en(wesel_13), .clk(CLK), .Q(ri_t13));  // open: clr
  Register #(.width(32)) register_23 (.D(Rwrite), .en(wesel_18), .clk(CLK), .Q(ri_t18));  // open: clr
  Register #(.width(32)) register_24 (.D(Rwrite), .en(wesel_23), .clk(CLK), .Q(ri_t23));  // open: clr
  Register #(.width(32)) register_25 (.D(Rwrite), .en(wesel_28), .clk(CLK), .Q(ri_t28));  // open: clr
  Demultiplexer #(.select(5)) demultiplexer_1 (
    .out0(wesel_0), .out1(wesel_1), .out2(wesel_2), .out3(wesel_3), .out4(wesel_4), .out5(wesel_5),
    .out6(wesel_6), .out7(wesel_7), .out8(wesel_8), .out9(wesel_9), .out10(wesel_10), .out11(wesel_11),
    .out12(wesel_12), .out13(wesel_13), .out14(wesel_14), .out15(wesel_15), .out16(wesel_16),
    .out17(wesel_17), .out18(wesel_18), .out19(wesel_19), .out20(wesel_20), .out21(wesel_21),
    .out22(wesel_22), .out23(wesel_23), .out24(wesel_24), .out25(wesel_25), .out26(wesel_26),
    .out27(wesel_27), .out28(wesel_28), .out29(wesel_29), .out30(wesel_30), .out31(wesel_31), .in(WE),
    .sel(rdesi));
  Register #(.width(32)) register_26 (.D(Rwrite), .en(wesel_4), .clk(CLK), .Q(ri_t4));  // open: clr
  Register #(.width(32)) register_27 (.D(Rwrite), .en(wesel_9), .clk(CLK), .Q(ri_t9));  // open: clr
  Register #(.width(32)) register_28 (.D(Rwrite), .en(wesel_14), .clk(CLK), .Q(ri_t14));  // open: clr
  Register #(.width(32)) register_29 (.D(Rwrite), .en(wesel_19), .clk(CLK), .Q(ri_t19));  // open: clr
  Register #(.width(32)) register_30 (.D(Rwrite), .en(wesel_24), .clk(CLK), .Q(ri_t24));  // open: clr
  Register #(.width(32)) register_31 (.D(Rwrite), .en(wesel_29), .clk(CLK), .Q(ri_t29));  // open: clr

  // Other names for the same wires on the sheet: clk_t = CLK; rdesi_t[4:0] = rdesi; rs1_t[31:0] = rs1;
  //   rs1i_t[4:0] = rs1i; rs2_t[31:0] = rs2; rs2i_t[4:0] = rs2i; rwrite_t[31:0] = Rwrite; we_t = WE
endmodule

module Imm_Gen (
  input  [31:0] Instruct,
  output [31:0] imm
);

  wire [2:0] pla_1_out;
  wire [3:0] b_splitter_1_b_imm_1_4;
  wire [4:0] s_splitter_1_s_imm_0_4;
  wire [5:0] b_splitter_1_b_imm_5_10;
  wire [6:0] s_splitter_1_s_imm_5_11;
  wire [7:0] j_splitter_1_j_imm_12_19;
  wire [9:0] j_splitter_1_j_imm_1_10;
  wire [11:0] i_splitter_1_i_imm0_11;
  wire [12:11] b_splitter_1_b_imm_11;
  wire [20:11] j_splitter_1_j_imm_11;
  wire [31:0] imm_b_t, imm_i_t, imm_j_t, imm_s_t;
  wire [31:12] imm_u_t;

  s_splitter s_splitter_1 (
    .Instruct(Instruct), .s_imm_0_4(s_splitter_1_s_imm_0_4), .s_imm_5_11(s_splitter_1_s_imm_5_11));  // open: s_opcode, s_funct3, s_rs1, s_rs2
  b_splitter b_splitter_1 (
    .Instruct(Instruct), .b_imm_1_4(b_splitter_1_b_imm_1_4), .b_imm_5_10(b_splitter_1_b_imm_5_10),
    .b_imm_11(b_splitter_1_b_imm_11[11]), .b_imm_12(b_splitter_1_b_imm_11[12]));  // open: b_opcode, b_funct3, b_rs1, b_rs2
  Multiplexer #(.select(3), .width(32)) multiplexer_1 (
    .in0(imm_i_t), .in1(imm_s_t), .in2(imm_b_t), .in3({imm_u_t, {12{1'b0}}}), .in4(imm_j_t), .out(imm),
    .sel(pla_1_out));  // open: in5, in6, in7
  PLA #(.in_width(7), .out_width(3), .\table ("0000011 000\n0010011 000\n1100111 000\n0100011 001\n1100011 010\n0110111 011\n0010111 011\n1101111 100")) pla_1 (
    .in(Instruct[6:0]), .out(pla_1_out));
  assign imm_s_t = {{20{s_splitter_1_s_imm_5_11[6]}}, {s_splitter_1_s_imm_5_11, s_splitter_1_s_imm_0_4}};  // Bit_Extender bit_extender_1
  assign imm_b_t = {{19{b_splitter_1_b_imm_11[12]}}, {b_splitter_1_b_imm_11, b_splitter_1_b_imm_5_10, b_splitter_1_b_imm_1_4, 1'b0}};  // Bit_Extender bit_extender_2
  i_splitter i_splitter_1 (
    .Instruct(Instruct), .i_imm0_11(i_splitter_1_i_imm0_11));  // open: opcode, i_rd, i_funct3, i_rs1
  j_splitter j_splitter_1 (
    .Instruct(Instruct), .j_imm_1_10(j_splitter_1_j_imm_1_10), .j_imm_11(j_splitter_1_j_imm_11[11]),
    .j_imm_12_19(j_splitter_1_j_imm_12_19), .j_imm_20(j_splitter_1_j_imm_11[20]));  // open: j_opcode, j_rd
  u_splitter u_splitter_1 (.Instruct(Instruct), .u_imm(imm_u_t));  // open: u_opcode, u_rd
  assign imm_i_t = {{20{i_splitter_1_i_imm0_11[11]}}, i_splitter_1_i_imm0_11};  // Bit_Extender bit_extender_3
  assign imm_j_t = {{11{j_splitter_1_j_imm_11[20]}}, {j_splitter_1_j_imm_11[20], j_splitter_1_j_imm_12_19, j_splitter_1_j_imm_11[11], j_splitter_1_j_imm_1_10, 1'b0}};  // Bit_Extender bit_extender_4

  // Other names for the same wires on the sheet: inst_t[31:0] = Instruct; opcode_t[6:0] = Instruct[6:0]
endmodule

module Program_Counter (
  input  [31:0] PC_in,
  input  Clock,
  input  reset,
  output [31:0] PC_next
);

  Register #(.width(32)) register_1 (.D(PC_in), .en(1'b1), .clk(Clock), .Q(PC_next), .clr(reset));
endmodule

module PC_plus4 (
  input  [31:0] PC_in,
  output [31:0] PC_plus_4
);

  Adder #(.width(32)) adder_1 (.a(PC_in), .b(32'h4), .out(PC_plus_4));  // open: cin, cout
endmodule

module ALU (
  input  [31:0] A,
  input  [31:0] B,
  input  [3:0] ALUSel,
  output [31:0] ALUOut
);

  wire comparator_1_lt, comparator_2_lt;
  wire [31:0] adder_1_out, and_1_out, bit_extender_1_out, bit_extender_2_out, or_1_out, shifter_1_out,
       shifter_2_out, shifter_3_out, subtractor_1_out, xor_1_out;

  Adder #(.width(32)) adder_1 (.a(A), .b(B), .out(adder_1_out));  // open: cin, cout
  Subtractor #(.width(32)) subtractor_1 (.a(A), .b(B), .out(subtractor_1_out));  // open: bin, bout
  assign and_1_out = A & B;  // AND_Gate and_1, 32 bits wide
  assign or_1_out = A | B;  // OR_Gate or_1, 32 bits wide
  assign xor_1_out = A ^ B;  // XOR_Gate xor_1, 32 bits wide
  Comparator #(.width(32)) comparator_1 (.a(A), .b(B), .lt(comparator_1_lt));  // open: gt, eq
  Comparator #(.mode("unsigned"), .width(32)) comparator_2 (.a(A), .b(B), .lt(comparator_2_lt));  // open: gt, eq
  Shifter #(.width(32)) shifter_1 (.in(A), .\dist (B[4:0]), .out(shifter_1_out));
  Shifter #(.shift("lr"), .width(32)) shifter_2 (.in(A), .\dist (B[4:0]), .out(shifter_2_out));
  Shifter #(.shift("ar"), .width(32)) shifter_3 (.in(A), .\dist (B[4:0]), .out(shifter_3_out));
  assign bit_extender_1_out = {{31{1'b0}}, comparator_1_lt};  // Bit_Extender bit_extender_1
  assign bit_extender_2_out = {{31{1'b0}}, comparator_2_lt};  // Bit_Extender bit_extender_2
  Multiplexer #(.select(4), .width(32)) multiplexer_1 (
    .in0(adder_1_out), .in1(shifter_1_out), .in2(bit_extender_1_out), .in3(bit_extender_2_out),
    .in4(xor_1_out), .in5(shifter_2_out), .in6(or_1_out), .in7(and_1_out), .in8(subtractor_1_out),
    .in13(shifter_3_out), .out(ALUOut), .sel(ALUSel));  // open: in9, in10, in11, in12, in14, in15

  // Other names for the same wires on the sheet: B_t[31:0] = B
endmodule

module Control (
  input  [6:0] op_code,
  input  [2:0] funct3,
  input  bltu,
  input  blt,
  input  beq,
  output [1:0] reg_write_sel,
  output imm_tk,
  output mem_we,
  output reg_we,
  output pc_tk,
  output branch_tk
);

  PLA #(.in_width(13), .out_width(7), .\table ("xxxxxx0110011 0010001\nxxxxxx0010011 0010101\nxxxxxx0000011 0010100\nxxxxxx0100011 0001100\nxxxxxx1101111 1110110\nxxxxxx1100111 1010110\nxxxxxx0110111 0010111\nxxxxxx0010111 0110101\n1xx0001100011 1100100\n0xx0011100011 1100100\nx1x1001100011 1100100\nx0x1011100011 1100100\nxx11101100011 1100100\nxx01111100011 1100100")) pla_1 (
    .in({beq, blt, bltu, funct3, op_code}), .out({branch_tk, pc_tk, reg_we, mem_we, imm_tk, reg_write_sel}));
endmodule

module ALU_Control (
  input  [6:0] opcode,
  input  [2:0] funct3,
  input  funct7,
  output [3:0] ALUSel
);

  PLA #(.in_width(11), .out_width(4), .\table ("0000011xxxx 0000\n0100011xxxx 0000\n1100011xxxx 0000\n0010011000x 0000\n0010011001x 0001\n0010011010x 0010\n0010011011x 0011\n0010011100x 0100\n00100111010 0101\n00100111011 1101\n0010011110x 0110\n0010011111x 0111\n01100110000 0000\n01100110001 1000\n0110011001x 0001\n0110011010x 0010\n0110011011x 0011\n0110011100x 0100\n01100111010 0101\n01100111011 1101\n0110011110x 0110\n0110011111x 0111")) pla_1 (
    .in({opcode, funct3, funct7}), .out(ALUSel));
endmodule

module Branch_Comp (
  input  [31:0] A,
  input  [31:0] B,
  output beq,
  output blt,
  output bltu
);

  Comparator #(.width(32)) comparator_1 (.a(A), .b(B), .eq(beq), .lt(blt));  // open: gt
  Comparator #(.mode("unsigned"), .width(32)) comparator_2 (.a(A), .b(B), .lt(bltu));  // open: gt, eq

  // Other names for the same wires on the sheet: A_t[31:0] = A; B_t[31:0] = B
endmodule

module Data_Mem (
  input  WE,
  input  CLK,
  input  [2:0] funct3,
  input  [31:0] Rwrite,
  input  [31:0] addr,
  output [31:0] rd_data
);

  wire [3:1] pla_1_out;
  wire [31:0] bit_extender_1_out, bit_extender_2_out, bit_extender_3_out, bit_extender_4_out, ram_1_dout,
       shifter_1_out, shifter_2_out;

  PLA #(.in_width(6), .out_width(4), .\table ("100100 0011\n100110 1100\n100000 0001\n100001 0010\n100010 0100\n100011 1000\nx010xx 0000")) pla_1 (
    .in({WE, funct3, addr[1:0]}), .out({pla_1_out, pla_1_out[1]}));
  RAM #(.addrWidth(16), .asyncread("true"), .byteenables("byteEnables"), .dataWidth(32)) ram_1 (
    .addr(addr[17:2]), .we(WE), .oe(1'b1), .clk(CLK), .din(shifter_1_out), .dout(ram_1_dout),
    .be3(pla_1_out[3]), .be2(pla_1_out[2]), .be1(pla_1_out[1]), .be0(pla_1_out[1]));
  Shifter #(.width(32)) shifter_1 (.in(Rwrite), .\dist ({addr[1:0], 3'b000}), .out(shifter_1_out));
  Shifter #(.shift("lr"), .width(32)) shifter_2 (.in(ram_1_dout), .\dist ({addr[1:0], 3'b000}), .out(shifter_2_out));
  assign bit_extender_1_out = {{16{shifter_2_out[15]}}, shifter_2_out[15:0]};  // Bit_Extender bit_extender_1
  assign bit_extender_2_out = {{16{1'b0}}, shifter_2_out[15:0]};  // Bit_Extender bit_extender_2
  assign bit_extender_3_out = {{24{shifter_2_out[7]}}, shifter_2_out[7:0]};  // Bit_Extender bit_extender_3
  assign bit_extender_4_out = {{24{1'b0}}, shifter_2_out[7:0]};  // Bit_Extender bit_extender_4
  Multiplexer #(.select(3), .width(32)) multiplexer_1 (
    .in0(bit_extender_3_out), .in1(bit_extender_1_out), .in2(shifter_2_out), .in4(bit_extender_4_out),
    .in5(bit_extender_2_out), .out(rd_data), .sel(funct3));  // open: in3, in6, in7
endmodule

module s_splitter (
  input  [31:0] Instruct,
  output [6:0] s_opcode,
  output [2:0] s_funct3,
  output [4:0] s_imm_0_4,
  output [4:0] s_rs1,
  output [6:0] s_imm_5_11,
  output [4:0] s_rs2
);


  assign s_funct3 = Instruct[14:12];
  assign s_imm_0_4 = Instruct[11:7];
  assign s_imm_5_11 = Instruct[31:25];
  assign s_opcode = Instruct[6:0];
  assign s_rs1 = Instruct[19:15];
  assign s_rs2 = Instruct[24:20];
endmodule

module i_splitter (
  input  [31:0] Instruct,
  output [6:0] opcode,
  output [4:0] i_rd,
  output [2:0] i_funct3,
  output [4:0] i_rs1,
  output [11:0] i_imm0_11
);


  assign i_funct3 = Instruct[14:12];
  assign i_imm0_11 = Instruct[31:20];
  assign i_rd = Instruct[11:7];
  assign i_rs1 = Instruct[19:15];
  assign opcode = Instruct[6:0];
endmodule

module b_splitter (
  input  [31:0] Instruct,
  output [6:0] b_opcode,
  output [3:0] b_imm_1_4,
  output [5:0] b_imm_5_10,
  output b_imm_11,
  output [2:0] b_funct3,
  output [4:0] b_rs1,
  output b_imm_12,
  output [4:0] b_rs2
);


  assign b_funct3 = Instruct[14:12];
  assign b_imm_1_4 = Instruct[11:8];
  assign b_imm_5_10 = Instruct[30:25];
  assign b_imm_11 = Instruct[7];
  assign b_imm_12 = Instruct[31];
  assign b_opcode = Instruct[6:0];
  assign b_rs1 = Instruct[19:15];
  assign b_rs2 = Instruct[24:20];
endmodule

module j_splitter (
  input  [31:0] Instruct,
  output [6:0] j_opcode,
  output [4:0] j_rd,
  output [9:0] j_imm_1_10,
  output j_imm_11,
  output [7:0] j_imm_12_19,
  output j_imm_20
);


  assign j_imm_1_10 = Instruct[30:21];
  assign j_imm_11 = Instruct[20];
  assign j_imm_12_19 = Instruct[19:12];
  assign j_imm_20 = Instruct[31];
  assign j_opcode = Instruct[6:0];
  assign j_rd = Instruct[11:7];
endmodule

module u_splitter (
  input  [31:0] Instruct,
  output [6:0] u_opcode,
  output [4:0] u_rd,
  output [19:0] u_imm
);


  assign u_imm = Instruct[31:12];
  assign u_opcode = Instruct[6:0];
  assign u_rd = Instruct[11:7];
endmodule
